# Fritzing sketch CENG317_PCB_DESIGN (saved by Fritzing 0.9.3b)
circuit board: 5.88986cm x 5.37928cm
breadboards: 1

parts:
  hc-sr1 = hc-sr04
  DHT1 = Humidity and Temperature Sensor DHT11
  Arduino_Uno_(Rev3)_-_ICSP = Arduino Uno (Rev3) - ICSP

nets:
  VCC: hc-sr1.VCC, DHT1.Vcc, Arduino_Uno_(Rev3)_-_ICSP.5V
  N1: hc-sr1.Trig, Arduino_Uno_(Rev3)_-_ICSP.ICSP_MOSI, Arduino_Uno_(Rev3)_-_ICSP.D11_PWM/MOSI
  N2: hc-sr1.Echo, Arduino_Uno_(Rev3)_-_ICSP.D12/MISO
  GND: hc-sr1.GND, DHT1.GND_1, Arduino_Uno_(Rev3)_-_ICSP.GND
  N3: DHT1.Data-signal, Arduino_Uno_(Rev3)_-_ICSP.D7

notes:
  Boswell Orendain

custom parts:
  Humidity and Temperature Sensor DHT11: Digital relative humidity & temperature sensor DHT11
